# Fritzing sketch ProbeCube_nano_v1 (saved by Fritzing 0.9.1b)
circuit board: 6.9cm x 4.9cm
breadboards: 1

parts:
  Arduino_Nano = Arduino Nano (Rev3.0)
  DHT22 = DHT22 Humidity and Temperature Sensor
  GP2Y1010AU0F1 = Header 6 [package=molex-1x6-ra]
  R9 = Resistor [tolerance=±5% resistance=220 package=THT]
  R1 = Resistor [tolerance=±5% resistance=10k package=THT]
  R2 = Resistor [tolerance=±5% resistance=150 package=THT]
  LED3 = LED - 3mm [color="Green (570nm)" package="3 mm [THT]"]
  R4 = Resistor [tolerance=±5% resistance=10k package=THT]
  TGSGD = female pin header, 2 pins [form="♀ (female)"]
  TGS5V = female pin header, 2 pins [form="♀ (female)"]
  LED2 = LED - 3mm [color="Orange (605nm)" package="3 mm [THT]"]
  LED1 = LED - 3mm [color="Red (633nm)" package="3 mm [THT]"]
  R8 = Resistor [tolerance=±5% resistance=220 package=THT]
  R7 = Resistor [tolerance=±5% resistance=220 package=THT]
  C1 = Electrolytic Capacitor [capacitance=0.22mF voltage=20V package="100 mil [THT, electrolytic]"]
  Soil = female pin header, 2 pins [form="♀ (female)"]
  R3 = Resistor [tolerance=±5% resistance=10k package=THT]
  CC3K1 = Adafruit CC3000 WiFi Breakout

nets:
  GND: Arduino_Nano.GND, DHT22.GND, GP2Y1010AU0F1.2, GP2Y1010AU0F1.4, R9.Pin_1, R4.Pin_0, TGSGD.pin1, R8.Pin_1, R7.Pin_1, C1.-, R3.Pin_1, CC3K1.GND
  N1: Arduino_Nano.D2, GP2Y1010AU0F1.3
  N2: Arduino_Nano.D3, CC3K1.IRQ
  N3: Arduino_Nano.D4, DHT22.DATA, R1.Pin_1
  N4: Arduino_Nano.D5, CC3K1.VBEN
  N5: Arduino_Nano.D7, LED1.anode
  N6: Arduino_Nano.D8, LED2.anode
  N7: Arduino_Nano.D9, LED3.anode
  N8: Arduino_Nano.D10, CC3K1.CS
  N9: Arduino_Nano.D11/MOSI, CC3K1.MOSI
  N10: Arduino_Nano.D12/MISO, CC3K1.MISO
  5V: Arduino_Nano.5V, DHT22.VDD, GP2Y1010AU0F1.6, R1.Pin_0, R2.Pin_0, TGS5V.pin1, TGS5V.pin2, Soil.pin2, CC3K1.VIN
  N11: Arduino_Nano.A2, R4.Pin_1, TGSGD.pin2
  N12: Arduino_Nano.A1, Soil.pin1, R3.Pin_0
  N13: Arduino_Nano.A0, GP2Y1010AU0F1.5
  N14: Arduino_Nano.D13/SCK, CC3K1.CLK
  N15: GP2Y1010AU0F1.1, R2.Pin_1, C1.+
  N16: R9.Pin_0, LED3.cathode
  N17: LED2.cathode, R8.Pin_0
  N18: LED1.cathode, R7.Pin_0

notes:
  https://github.com/Lafudoci/ProbeCube
  ProbeCube Project
  Model: Nano v1.0
  CC3000
  Arduino Nano
  GP2Y1010AU0F

custom parts:
  Adafruit CC3000 WiFi Breakout: CC3000 WiFi Breakout
