# Fritzing sketch ProbeCube_shield_v1 (saved by Fritzing 0.9.1b)
circuit board: 6.88566cm x 5.36311cm
breadboards: 1

parts:
  DHT22 = DHT22 Humidity and Temperature Sensor
  GP2Y1010AU0F1 = Header 6 [package=molex-1x6-ra]
  R9 = Resistor [tolerance=±5% resistance=220 package=THT]
  R1 = Resistor [tolerance=±5% resistance=10k package=THT]
  R2 = Resistor [tolerance=±5% resistance=150 package=THT]
  LED3 = LED - 3mm [color="Green (570nm)" package="3 mm [THT]"]
  R4 = Resistor [tolerance=±5% resistance=10k package=THT]
  TGSGD = female pin header, 2 pins [form="♀ (female)"]
  TGS5V = female pin header, 2 pins [form="♀ (female)"]
  LED2 = LED - 3mm [color="Yellow (595nm)" package="3 mm [THT]"]
  LED1 = LED - 3mm [color="Red (633nm)" package="3 mm [THT]"]
  R8 = Resistor [tolerance=±5% resistance=220 package=THT]
  R7 = Resistor [tolerance=±5% resistance=220 package=THT]
  C1 = Electrolytic Capacitor [capacitance=0.22mF voltage=20V package="100 mil [THT, electrolytic]"]
  R3 = Resistor [tolerance=±5% resistance=10k package=THT]
  CC3K1 = Adafruit CC3000 WiFi Breakout
  元件1 = Arduino Uno (Rev3)
  Reset = Pushbutton [package=THT]
  Soil = female pin header, 2 pins [form="♀ (female)"]

nets:
  VDD: DHT22.VDD, GP2Y1010AU0F1.6, R1.Pin_0, R2.Pin_0, TGS5V.pin1, TGS5V.pin2, CC3K1.VIN, 元件1.5V, Soil.pin2
  N1: DHT22.DATA, R1.Pin_1, 元件1.D4
  GND: DHT22.GND, GP2Y1010AU0F1.2, GP2Y1010AU0F1.4, R9.Pin_1, R4.Pin_0, TGSGD.pin1, R8.Pin_1, R7.Pin_1, C1.-, R3.Pin_1, CC3K1.GND, 元件1.GND, Reset.leg0
  N2: GP2Y1010AU0F1.1, R2.Pin_1, C1.+
  N3: GP2Y1010AU0F1.3, 元件1.D2
  N4: GP2Y1010AU0F1.5, 元件1.A0
  N5: R9.Pin_0, LED3.cathode
  N6: LED3.anode, 元件1.D9_PWM
  N7: R4.Pin_1, TGSGD.pin2, 元件1.A2
  N8: LED2.cathode, R8.Pin_0
  N9: LED2.anode, 元件1.D8
  N10: LED1.cathode, R7.Pin_0
  N11: LED1.anode, 元件1.D7
  N12: R3.Pin_0, 元件1.A1, Soil.pin1
  N13: CC3K1.CLK, 元件1.D13/SCK
  N14: CC3K1.MISO, 元件1.D12/MISO
  N15: CC3K1.MOSI, 元件1.D11_PWM/MOSI
  N16: CC3K1.CS, 元件1.D10_PWM/SS
  N17: CC3K1.VBEN, 元件1.D5_PWM
  N18: CC3K1.IRQ, 元件1.D3_PWM
  N19: 元件1.RESET, Reset.leg1

notes:
  https://github.com/Lafudoci/ProbeCube
  ProbeCube Project
  Model: Shield v1.0
  CC3000
  GP2Y1010AU0F

custom parts:
  Adafruit CC3000 WiFi Breakout: CC3000 WiFi Breakout
