# Fritzing sketch ProbeCube_gieger (saved by Fritzing 0.9.1b)
circuit board: 6.88566cm x 5.36311cm
breadboards: 1

parts:
  DHT22 = DHT22 Humidity and Temperature Sensor
  R9 = Resistor [tolerance=±5% resistance=220 package=THT]
  R1 = Resistor [tolerance=±5% resistance=10k package=THT]
  LED3 = LED - 3mm [color="Green (570nm)" package="3 mm [THT]"]
  R4 = Resistor [tolerance=±5% resistance=10k package=THT]
  TGSGD = female pin header, 2 pins [form="♀ (female)"]
  TGS5V = female pin header, 2 pins [form="♀ (female)"]
  LED2 = LED - 3mm [color="Yellow (595nm)" package="3 mm [THT]"]
  LED1 = LED - 3mm [color="Red (633nm)" package="3 mm [THT]"]
  R8 = Resistor [tolerance=±5% resistance=220 package=THT]
  R7 = Resistor [tolerance=±5% resistance=220 package=THT]
  R3 = Resistor [tolerance=±5% resistance=10k package=THT]
  CC3K1 = Adafruit CC3000 WiFi Breakout
  元件1 = Arduino Uno (Rev3)
  Reset = Pushbutton [package=THT]
  Soil = female pin header, 2 pins [form="♀ (female)"]
  J1 = female pin header, 5 pins [form="♀ (female)"]

nets:
  VDD: DHT22.VDD, R1.Pin_0, TGS5V.pin1, TGS5V.pin2, CC3K1.VIN, 元件1.5V, Soil.pin2, J1.pin1
  N1: DHT22.DATA, R1.Pin_1, 元件1.D4
  GND: DHT22.GND, R9.Pin_1, R4.Pin_0, TGSGD.pin1, R8.Pin_1, R7.Pin_1, R3.Pin_1, CC3K1.GND, 元件1.GND, Reset.leg0, J1.pin2
  N2: R9.Pin_0, LED3.cathode
  N3: LED3.anode, 元件1.D9_PWM
  N4: R4.Pin_1, TGSGD.pin2, 元件1.A2
  N5: LED2.cathode, R8.Pin_0
  N6: LED2.anode, 元件1.D8
  N7: LED1.cathode, R7.Pin_0
  N8: LED1.anode, 元件1.D7
  N9: R3.Pin_0, 元件1.A1, Soil.pin1
  N10: CC3K1.CLK, 元件1.D13/SCK
  N11: CC3K1.MISO, 元件1.D12/MISO
  N12: CC3K1.MOSI, 元件1.D11_PWM/MOSI
  N13: CC3K1.CS, 元件1.D10_PWM/SS
  N14: CC3K1.VBEN, 元件1.D5_PWM
  N15: CC3K1.IRQ, 元件1.D3_PWM
  N16: 元件1.D2, J1.pin3
  N17: 元件1.D6_PWM, J1.pin5
  N18: 元件1.RESET, Reset.leg1

notes:
  https://github.com/Lafudoci/ProbeCube
  ProbeCube Project
  Model: Shield v1.0
  CC3000
  GP2Y1010AU0F

custom parts:
  Adafruit CC3000 WiFi Breakout: CC3000 WiFi Breakout
