# Fritzing sketch ProbeCube_v099_20160223 (saved by Fritzing 0.9.2b)
circuit board: 4.4cm x 4.3cm
breadboards: 1

parts:
  DHT22 = DHT22 Humidity and Temperature Sensor
  R1_10k = Resistor [tolerance=±5% resistance=10k package=THT]
  R2_10k = Resistor [tolerance=±5% resistance=10k package=THT]
  tgs2602-5V = female pin header, 2 pins [form="♀ (female)"]
  tgs2602-GD = female pin header, 2 pins [form="♀ (female)"]
  G3 = female pin header, 8 pins [form="♀ (female)"]
  J6 = female pin header, 11 pins [form="♀ (female)"]
  J9 = female pin header, 12 pins [form="♀ (female)"]
  J7 = female pin header, 10 pins [form="♀ (female)"]
  J10 = female pin header, 1 pin [form="♀ (female)"]
  J11 = female pin header, 12 pins [form="♀ (female)"]

nets:
  N1: DHT22.VDD, R1_10k.Pin_0, J9.pin12, J7.pin10
  N2: DHT22.DATA, R1_10k.Pin_1, J9.pin2
  N3: DHT22.GND, R2_10k.Pin_1, tgs2602-GD.pin2, G3.pin2, G3.pin3, J6.pin10, J9.pin9, J7.pin7, J11.pin11
  N4: R2_10k.Pin_0, tgs2602-GD.pin1, J11.pin1
  N5: tgs2602-5V.pin1, tgs2602-5V.pin2, G3.pin1, J6.pin11, J11.pin12
  N6: G3.pin4, J6.pin9, J11.pin10
  N7: G3.pin5, J6.pin8, J11.pin9
  N8: J6.pin1, J11.pin2
  N9: J6.pin2, J11.pin3
  N10: J6.pin3, J11.pin4
  N11: J6.pin4, J11.pin5
  N12: J6.pin5, J11.pin6
  N13: J6.pin6, J11.pin7
  N14: J6.pin7, J11.pin8
  N15: J9.pin1, J10.pin1
  N16: J9.pin3, J7.pin1
  N17: J9.pin4, J7.pin2
  N18: J9.pin5, J7.pin3
  N19: J9.pin6, J7.pin4
  N20: J9.pin7, J7.pin5
  N21: J9.pin8, J7.pin6
  N22: J9.pin10, J7.pin8
  N23: J9.pin11, J7.pin9

notes:
  DHT22
  D1
  >
  http://www.3203.info
  /  /  /  /  /  /  /  /  /  /  /
  wifi atena<--Photon-->microUSB
