# Fritzing sketch ProbeCube_v099_20160225_bread (saved by Fritzing 0.9.2b)
breadboards: 1

parts:
  G3 = female pin header, 8 pins [form="♀ (female)"]
  R1 = Resistor [tolerance=±5% resistance=10k package=THT]
  DHT1 = DHT22 Humidity and Temperature Sensor
  R2 = Resistor [tolerance=±5% resistance=10k package=THT]
  元件1 = Photon
  Figaro_TGS_2602_Gas_Sensor1 = Figaro TGS 2602 Gas Sensor

nets:
  VDD: G3.pin1, DHT1.VDD, R2.Pin_0, 元件1.VIN, Figaro_TGS_2602_Gas_Sensor1.pin_3, Figaro_TGS_2602_Gas_Sensor1.pin_4
  GND: G3.pin2, R1.Pin_0, DHT1.GND, 元件1.GND, Figaro_TGS_2602_Gas_Sensor1.pin_1
  N1: G3.pin4, 元件1.TX
  N2: G3.pin5, 元件1.RX
  N3: R1.Pin_1, 元件1.A0, Figaro_TGS_2602_Gas_Sensor1.pin_2
  N4: DHT1.DATA, R2.Pin_1, 元件1.D2

custom parts:
  Figaro TGS 2602 Gas Sensor: The sensing element is comprised of a metal oxide semiconductor layer formed on the alumina substrate of a sensing chip together with an integrated heater. In the presence of detectable gas, sensor conductivity increases depending on gas concentration in the air. A simple electrical circuit can convert the change in conductivity to an output signal which corresponds to the gas concentration.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
